// Logisim project selector41_4.circ as structural Verilog: 1 circuit, main circuit main
module main (
  input  in_1,
  input  in_2,
  input  [3:0] in_3,
  input  [3:0] in_4,
  input  [3:0] in_5,
  input  [3:0] in_6,
  output [3:0] out_7
);

  wire [3:0] and_1_out, and_2_out, and_3_out, and_4_out, bit_extender_1_out, bit_extender_2_out, not_1_out,
       not_2_out, not_3_out, not_4_out;

  assign bit_extender_1_out = {{3{in_1}}, in_1};  // Bit_Extender bit_extender_1
  assign bit_extender_2_out = {{3{in_2}}, in_2};  // Bit_Extender bit_extender_2
  assign not_1_out = ~bit_extender_1_out;  // NOT_Gate not_1, 4 bits wide
  assign not_2_out = ~bit_extender_2_out;  // NOT_Gate not_2, 4 bits wide
  assign not_3_out = ~bit_extender_1_out;  // NOT_Gate not_3, 4 bits wide
  assign not_4_out = ~bit_extender_2_out;  // NOT_Gate not_4, 4 bits wide
  assign and_1_out = not_1_out & in_3 & not_2_out;  // AND_Gate and_1, 4 bits wide
  assign and_2_out = not_3_out & in_4 & bit_extender_2_out;  // AND_Gate and_2, 4 bits wide
  assign and_3_out = bit_extender_1_out & in_5 & not_4_out;  // AND_Gate and_3, 4 bits wide
  assign and_4_out = bit_extender_1_out & in_6 & bit_extender_2_out;  // AND_Gate and_4, 4 bits wide
  assign out_7 = and_1_out | and_2_out | and_3_out | and_4_out;  // OR_Gate or_1, 4 bits wide
endmodule
