// Logisim project decoder.circ as structural Verilog: 1 circuit, main circuit main
module main (
  input  D2,
  input  D1,
  input  D0,
  input  G1,
  input  G2,
  output NOT_Y0,
  output NOT_Y1,
  output NOT_Y2,
  output NOT_Y3,
  output NOT_Y4,
  output NOT_Y5,
  output NOT_Y6,
  output NOT_Y7
);

  wire not_1_out, not_2_out, not_3_out, not_4_out;

  not not_1 (not_1_out, D2);
  not not_2 (not_2_out, D1);
  not not_3 (not_3_out, D0);
  not not_4 (not_4_out, G2);
  nand nand_1 (NOT_Y0, G1, not_1_out, not_2_out, not_3_out, not_4_out);
  nand nand_2 (NOT_Y1, G1, not_1_out, not_2_out, D0, not_4_out);
  nand nand_3 (NOT_Y2, G1, not_1_out, D1, not_3_out, not_4_out);
  nand nand_4 (NOT_Y3, G1, not_1_out, D1, D0, not_4_out);
  nand nand_5 (NOT_Y4, G1, D2, not_2_out, not_3_out, not_4_out);
  nand nand_6 (NOT_Y5, G1, D2, not_2_out, D0, not_4_out);
  nand nand_7 (NOT_Y6, G1, D2, D1, not_3_out, not_4_out);
  nand nand_8 (NOT_Y7, G1, D2, D1, D0, not_4_out);
endmodule
