// Logisim project encoder83.circ as structural Verilog: 1 circuit, main circuit main
module main (
  input  D7,
  input  D6,
  input  D5,
  input  D4,
  input  D3,
  input  D2,
  input  D1,
  input  D0,
  output Y2,
  output Y1,
  output Y0
);

  wire and_1_out, and_2_out, and_3_out, and_4_out, and_5_out, and_6_out, and_7_out, and_8_out, and_9_out,
       and_10_out, and_11_out, and_12_out, and_13_out, and_14_out, and_15_out, not_1_out, not_2_out,
       not_3_out, not_4_out, not_5_out, not_6_out, not_7_out, not_8_out, or_1_out, or_2_out, or_3_out;

  not not_1 (not_1_out, D7);
  not not_2 (not_2_out, D6);
  not not_3 (not_3_out, D5);
  not not_4 (not_4_out, D4);
  not not_5 (not_5_out, D3);
  not not_6 (not_6_out, D2);
  not not_7 (not_7_out, D1);
  not not_8 (not_8_out, D0);
  and and_1 (and_1_out, not_5_out, not_6_out, not_7_out, not_8_out);
  and and_2 (and_2_out, not_3_out, not_4_out, not_7_out, not_8_out);
  and and_3 (and_3_out, not_2_out, not_4_out, not_6_out, not_8_out);
  and and_4 (and_4_out, D7, not_2_out, not_3_out, not_4_out);
  and and_5 (and_5_out, not_1_out, D6, not_3_out, not_4_out);
  and and_6 (and_6_out, not_1_out, not_2_out, D5, not_4_out);
  and and_7 (and_7_out, not_1_out, not_2_out, not_3_out, D4);
  and and_8 (and_8_out, D7, not_2_out, not_5_out, not_6_out);
  and and_9 (and_9_out, not_1_out, D6, not_5_out, not_6_out);
  and and_10 (and_10_out, not_1_out, not_2_out, D3, not_6_out);
  and and_11 (and_11_out, not_1_out, not_2_out, not_5_out, D2);
  and and_12 (and_12_out, D7, not_3_out, not_5_out, not_7_out);
  and and_13 (and_13_out, not_1_out, D5, not_5_out, not_7_out);
  and and_14 (and_14_out, not_1_out, not_3_out, D3, not_7_out);
  and and_15 (and_15_out, not_1_out, not_3_out, not_5_out, D1);
  or or_1 (or_1_out, and_4_out, and_5_out, and_6_out, and_7_out);
  or or_2 (or_2_out, and_8_out, and_9_out, and_10_out, and_11_out);
  or or_3 (or_3_out, and_12_out, and_13_out, and_14_out, and_15_out);
  and and_16 (Y2, or_1_out, and_1_out);
  and and_17 (Y1, or_2_out, and_2_out);
  and and_18 (Y0, or_3_out, and_3_out);
endmodule
