// Logisim project Regfiles.circ as structural Verilog: 1 circuit, main circuit main
module main (
  input  [3:0] wdata,
  input  we,
  input  [3:0] waddr,
  input  rst,
  input  [3:0] raddr1,
  input  [3:0] raddr2,
  output [3:0] rdata1,
  output [3:0] rdata2
);

  wire clock_1_out, demultiplexer_1_out0, demultiplexer_1_out1, demultiplexer_1_out2, demultiplexer_1_out3,
       demultiplexer_1_out4, demultiplexer_1_out5, demultiplexer_1_out6, demultiplexer_1_out7,
       demultiplexer_1_out8, demultiplexer_1_out9, demultiplexer_1_out10, demultiplexer_1_out11,
       demultiplexer_1_out12, demultiplexer_1_out13, demultiplexer_1_out14, demultiplexer_1_out15, not_1_out;
  wire [3:0] register_1_q, register_2_q, register_3_q, register_4_q, register_5_q, register_6_q,
       register_7_q, register_8_q, register_9_q, register_10_q, register_11_q, register_12_q, register_13_q,
       register_14_q, register_15_q, register_16_q;

  Clock clock_1 (.out(clock_1_out));
  Demultiplexer #(.select(4)) demultiplexer_1 (
    .out0(demultiplexer_1_out0), .out1(demultiplexer_1_out1), .out2(demultiplexer_1_out2),
    .out3(demultiplexer_1_out3), .out4(demultiplexer_1_out4), .out5(demultiplexer_1_out5),
    .out6(demultiplexer_1_out6), .out7(demultiplexer_1_out7), .out8(demultiplexer_1_out8),
    .out9(demultiplexer_1_out9), .out10(demultiplexer_1_out10), .out11(demultiplexer_1_out11),
    .out12(demultiplexer_1_out12), .out13(demultiplexer_1_out13), .out14(demultiplexer_1_out14),
    .out15(demultiplexer_1_out15), .in(1'b1), .sel(waddr), .en(we));
  not not_1 (not_1_out, we);
  Register #(.width(4), .trigger("falling")) register_1 (
    .D(wdata), .en(demultiplexer_1_out0), .Q(register_1_q), .clk(clock_1_out), .clr(rst));
  Register #(.width(4), .trigger("falling")) register_2 (
    .D(wdata), .en(demultiplexer_1_out2), .Q(register_2_q), .clk(clock_1_out), .clr(rst));
  Register #(.width(4), .trigger("falling")) register_3 (
    .D(wdata), .en(demultiplexer_1_out4), .Q(register_3_q), .clk(clock_1_out), .clr(rst));
  Register #(.width(4), .trigger("falling")) register_4 (
    .D(wdata), .en(demultiplexer_1_out6), .Q(register_4_q), .clk(clock_1_out), .clr(rst));
  Register #(.width(4), .trigger("falling")) register_5 (
    .D(wdata), .en(demultiplexer_1_out8), .Q(register_5_q), .clk(clock_1_out), .clr(rst));
  Register #(.width(4), .trigger("falling")) register_6 (
    .D(wdata), .en(demultiplexer_1_out10), .Q(register_6_q), .clk(clock_1_out), .clr(rst));
  Register #(.width(4), .trigger("falling")) register_7 (
    .D(wdata), .en(demultiplexer_1_out12), .Q(register_7_q), .clk(clock_1_out), .clr(rst));
  Register #(.width(4), .trigger("falling")) register_8 (
    .D(wdata), .en(demultiplexer_1_out14), .Q(register_8_q), .clk(clock_1_out), .clr(rst));
  Register #(.width(4), .trigger("falling")) register_9 (
    .D(wdata), .en(demultiplexer_1_out1), .Q(register_9_q), .clk(clock_1_out), .clr(rst));
  Register #(.width(4), .trigger("falling")) register_10 (
    .D(wdata), .en(demultiplexer_1_out3), .Q(register_10_q), .clk(clock_1_out), .clr(rst));
  Register #(.width(4), .trigger("falling")) register_11 (
    .D(wdata), .en(demultiplexer_1_out5), .Q(register_11_q), .clk(clock_1_out), .clr(rst));
  Register #(.width(4), .trigger("falling")) register_12 (
    .D(wdata), .en(demultiplexer_1_out7), .Q(register_12_q), .clk(clock_1_out), .clr(rst));
  Register #(.width(4), .trigger("falling")) register_13 (
    .D(wdata), .en(demultiplexer_1_out9), .Q(register_13_q), .clk(clock_1_out), .clr(rst));
  Register #(.width(4), .trigger("falling")) register_14 (
    .D(wdata), .en(demultiplexer_1_out11), .Q(register_14_q), .clk(clock_1_out), .clr(rst));
  Register #(.width(4), .trigger("falling")) register_15 (
    .D(wdata), .en(demultiplexer_1_out13), .Q(register_15_q), .clk(clock_1_out), .clr(rst));
  Register #(.width(4), .trigger("falling")) register_16 (
    .D(wdata), .en(demultiplexer_1_out15), .Q(register_16_q), .clk(clock_1_out), .clr(rst));
  Multiplexer #(.select(4), .width(4)) multiplexer_1 (
    .in0(register_1_q), .in1(register_9_q), .in2(register_2_q), .in3(register_10_q), .in4(register_3_q),
    .in5(register_11_q), .in6(register_4_q), .in7(register_12_q), .in8(register_5_q), .in9(register_13_q),
    .in10(register_6_q), .in11(register_14_q), .in12(register_7_q), .in13(register_15_q),
    .in14(register_8_q), .in15(register_16_q), .out(rdata1), .sel(raddr1), .en(not_1_out));
  Multiplexer #(.select(4), .width(4)) multiplexer_2 (
    .in0(register_1_q), .in1(register_9_q), .in2(register_2_q), .in3(register_10_q), .in4(register_3_q),
    .in5(register_11_q), .in6(register_4_q), .in7(register_12_q), .in8(register_5_q), .in9(register_13_q),
    .in10(register_6_q), .in11(register_14_q), .in12(register_7_q), .in13(register_15_q),
    .in14(register_8_q), .in15(register_16_q), .out(rdata2), .sel(raddr2), .en(not_1_out));

  // Notes on the sheet:
  //   CLK
endmodule
